// Logisim project 16 Bits Adder.circ as structural Verilog: 5 circuits, main circuit SomadorCompleto
module Somador (
  input  [15:0] A,
  input  [15:0] B,
  output Carry,
  output [15:0] Saida
);

  wire full_adder_1_carry_out, full_adder_2_carry_out, full_adder_3_carry_out, full_adder_4_carry_out,
       full_adder_5_carry_out, full_adder_6_carry_out, full_adder_7_carry_out, full_adder_8_carry_out,
       full_adder_9_carry_out, full_adder_10_carry_out, full_adder_11_carry_out, full_adder_12_carry_out,
       full_adder_13_carry_out, full_adder_14_carry_out, half_adder_1_carry;

  Full_Adder full_adder_1 (
    .A(B[1]), .B(A[1]), .Carry(half_adder_1_carry), .Saida(Saida[1]), .Carry_Out(full_adder_1_carry_out));
  Half_Adder half_adder_1 (.in_1(B[0]), .in_2(A[0]), .Saida(Saida[0]), .Carry(half_adder_1_carry));
  Full_Adder full_adder_2 (
    .A(B[2]), .B(A[2]), .Carry(full_adder_1_carry_out), .Saida(Saida[2]), .Carry_Out(full_adder_2_carry_out));
  Full_Adder full_adder_3 (
    .A(B[4]), .B(A[4]), .Carry(full_adder_4_carry_out), .Saida(Saida[4]), .Carry_Out(full_adder_3_carry_out));
  Full_Adder full_adder_4 (
    .A(B[3]), .B(A[3]), .Carry(full_adder_2_carry_out), .Saida(Saida[3]), .Carry_Out(full_adder_4_carry_out));
  Full_Adder full_adder_5 (
    .A(B[6]), .B(A[6]), .Carry(full_adder_6_carry_out), .Saida(Saida[6]), .Carry_Out(full_adder_5_carry_out));
  Full_Adder full_adder_6 (
    .A(B[5]), .B(A[5]), .Carry(full_adder_3_carry_out), .Saida(Saida[5]), .Carry_Out(full_adder_6_carry_out));
  Full_Adder full_adder_7 (
    .A(B[7]), .B(A[7]), .Carry(full_adder_5_carry_out), .Saida(Saida[7]), .Carry_Out(full_adder_7_carry_out));
  Full_Adder full_adder_8 (
    .A(B[8]), .B(A[8]), .Carry(full_adder_7_carry_out), .Saida(Saida[8]), .Carry_Out(full_adder_8_carry_out));
  Full_Adder full_adder_9 (
    .A(B[9]), .B(A[9]), .Carry(full_adder_8_carry_out), .Saida(Saida[9]), .Carry_Out(full_adder_9_carry_out));
  Full_Adder full_adder_10 (
    .A(B[11]), .B(A[11]), .Carry(full_adder_11_carry_out), .Saida(Saida[11]),
    .Carry_Out(full_adder_10_carry_out));
  Full_Adder full_adder_11 (
    .A(B[10]), .B(A[10]), .Carry(full_adder_9_carry_out), .Saida(Saida[10]),
    .Carry_Out(full_adder_11_carry_out));
  Full_Adder full_adder_12 (
    .A(B[12]), .B(A[12]), .Carry(full_adder_10_carry_out), .Saida(Saida[12]),
    .Carry_Out(full_adder_12_carry_out));
  Full_Adder full_adder_13 (
    .A(B[14]), .B(A[14]), .Carry(full_adder_14_carry_out), .Saida(Saida[14]),
    .Carry_Out(full_adder_13_carry_out));
  Full_Adder full_adder_14 (
    .A(B[13]), .B(A[13]), .Carry(full_adder_12_carry_out), .Saida(Saida[13]),
    .Carry_Out(full_adder_14_carry_out));
  Full_Adder full_adder_15 (
    .A(B[15]), .B(A[15]), .Carry(full_adder_13_carry_out), .Saida(Saida[15]), .Carry_Out(Carry));
endmodule

// Half
module Half_Adder (
  input  in_1,
  input  in_2,
  output Saida,
  output Carry
);

  and and_1 (Carry, in_1, in_2);
  xor xor_1 (Saida, in_1, in_2);
endmodule

module Full_Adder (
  input  A,
  input  B,
  input  Carry,
  output Saida,
  output Carry_Out
);

  wire and_1_out, half_adder_1_carry, half_adder_1_saida;

  Half_Adder half_adder_1 (.in_1(A), .in_2(B), .Saida(half_adder_1_saida), .Carry(half_adder_1_carry));
  and and_1 (and_1_out, half_adder_1_saida, Carry);
  xor xor_1 (Saida, half_adder_1_saida, Carry);
  or or_1 (Carry_Out, and_1_out, half_adder_1_carry);
endmodule

module Complemento2 (
  input  [15:0] A,
  input  Seletor,
  output CarryOut,
  output [15:0] Saida
);

  wire somador_1_carry;
  wire [15:0] not_1_out, somador_1_saida;

  assign not_1_out = ~A;  // NOT_Gate not_1, 16 bits wide
  Somador somador_1 (.A(16'h1), .B(not_1_out), .Carry(somador_1_carry), .Saida(somador_1_saida));
  Multiplexer #(.enable("false")) multiplexer_1 (.in0(1'b0), .in1(somador_1_carry), .out(CarryOut), .sel(Seletor));
  Multiplexer #(.width(16), .enable("false")) multiplexer_2 (
    .in0(A), .in1(somador_1_saida), .out(Saida), .sel(Seletor));
endmodule

module SomadorCompleto (
  input  [15:0] A,
  input  [15:0] B,
  input  Seletor_A,
  input  Seletor_B,
  output CarryComp2_A,
  output Carry,
  output CarryComp2_B,
  output [15:0] Saida
);

  wire [15:0] complemento2_1_saida, complemento2_2_saida;

  Complemento2 complemento2_1 (.A(A), .Seletor(Seletor_A), .CarryOut(CarryComp2_A), .Saida(complemento2_1_saida));
  Complemento2 complemento2_2 (.A(B), .Seletor(Seletor_B), .CarryOut(CarryComp2_B), .Saida(complemento2_2_saida));
  Somador somador_1 (.A(complemento2_1_saida), .B(complemento2_2_saida), .Carry(Carry), .Saida(Saida));
endmodule
