// Logisim project Filtro.circ as structural Verilog: 1 circuit, main circuit main
module main (
  input  [7:0] x_n,
  input  in_2,
  input  in_3,
  input  in_4,
  input  in_5,
  input  in_6,
  input  in_7,
  input  in_8,
  output out_9,
  output CarryOut,
  output out_11,
  output [15:0] y_n
);

  wire undriven;
  wire [7:0] ram_1_data, rom_1_data;
  wire [15:0] bit_extender_1_out, bit_extender_2_out, multiplier_1_cout, multiplier_1_out, register_1_q;

  // Probe on ram_1_data
  RAM #(.addrWidth(4), .bus("separate")) ram_1 (
    .addr(4'b0000), .din(x_n), .data(ram_1_data), .str(in_3), .sel(in_5), .clk(in_2), .ld(in_5));  // open: clr
  ROM #(.addrWidth(4)) rom_1 (.addr(4'b0000), .data(rom_1_data), .sel(undriven));
  assign bit_extender_1_out = {{8{1'b0}}, ram_1_data};  // Bit_Extender bit_extender_1
  // Probe on rom_1_data
  assign bit_extender_2_out = {{8{1'b0}}, rom_1_data};  // Bit_Extender bit_extender_2
  Clock clock_1 ();  // open: out
  // Probe on multiplier_1_out
  Multiplier #(.width(16)) multiplier_1 (
    .a(bit_extender_1_out), .b(bit_extender_2_out), .out(multiplier_1_out), .cin({16{1'b0}}),
    .cout(multiplier_1_cout));
  SomadorCompleto somadorcompleto_1 (
    .A(multiplier_1_out), .B(register_1_q), .Seletor_A(in_4), .Seletor_B(in_4), .CarryComp2_A(out_11),
    .CarryComp2_B(out_9), .Carry(CarryOut), .Saida(y_n));
  Register #(.width(16)) register_1 (.D(y_n), .en(in_7), .Q(register_1_q), .clk(in_8));  // open: clr

  // Notes on the sheet:
  //   contents of rom_1 (hex, n*v repeats v):
  //   31
endmodule
