// Logisim project lab2.circ as structural Verilog: 6 circuits, main circuit MAC
module half_adder (
  input  A,
  input  B,
  output Saida,
  output Cout
);

  xor xor_1 (Saida, A, B);
  and and_1 (Cout, A, B);
endmodule

module full_adder (
  input  A,
  input  B,
  input  Cin,
  output Saida,
  output Cout
);

  wire and_1_out, and_2_out, xor_1_out;

  xor xor_1 (xor_1_out, A, B);
  xor xor_2 (Saida, xor_1_out, Cin);
  and and_1 (and_1_out, xor_1_out, Cin);
  and and_2 (and_2_out, A, B);
  or or_1 (Cout, and_1_out, and_2_out);
endmodule

module somador (
  input  [15:0] A,
  input  [15:0] B,
  output Carry,
  output [15:0] Sum
);

  wire full_adder_1_cout, full_adder_2_cout, full_adder_3_cout, full_adder_4_cout, full_adder_5_cout,
       full_adder_6_cout, full_adder_7_cout, full_adder_8_cout, full_adder_9_cout, full_adder_10_cout,
       full_adder_11_cout, full_adder_12_cout, full_adder_13_cout, full_adder_14_cout, half_adder_1_cout;

  half_adder half_adder_1 (.A(B[0]), .B(A[0]), .Saida(Sum[0]), .Cout(half_adder_1_cout));
  full_adder full_adder_1 (.A(B[2]), .B(A[2]), .Cin(full_adder_2_cout), .Saida(Sum[2]), .Cout(full_adder_1_cout));
  full_adder full_adder_2 (.A(B[1]), .B(A[1]), .Cin(half_adder_1_cout), .Saida(Sum[1]), .Cout(full_adder_2_cout));
  full_adder full_adder_3 (.A(B[3]), .B(A[3]), .Cin(full_adder_1_cout), .Saida(Sum[3]), .Cout(full_adder_3_cout));
  full_adder full_adder_4 (.A(B[4]), .B(A[4]), .Cin(full_adder_3_cout), .Saida(Sum[4]), .Cout(full_adder_4_cout));
  full_adder full_adder_5 (.A(B[5]), .B(A[5]), .Cin(full_adder_4_cout), .Saida(Sum[5]), .Cout(full_adder_5_cout));
  full_adder full_adder_6 (.A(B[6]), .B(A[6]), .Cin(full_adder_5_cout), .Saida(Sum[6]), .Cout(full_adder_6_cout));
  full_adder full_adder_7 (.A(B[8]), .B(A[8]), .Cin(full_adder_8_cout), .Saida(Sum[8]), .Cout(full_adder_7_cout));
  full_adder full_adder_8 (.A(B[7]), .B(A[7]), .Cin(full_adder_6_cout), .Saida(Sum[7]), .Cout(full_adder_8_cout));
  full_adder full_adder_9 (.A(B[9]), .B(A[9]), .Cin(full_adder_7_cout), .Saida(Sum[9]), .Cout(full_adder_9_cout));
  full_adder full_adder_10 (.A(B[10]), .B(A[10]), .Cin(full_adder_9_cout), .Saida(Sum[10]), .Cout(full_adder_10_cout));
  full_adder full_adder_11 (.A(B[11]), .B(A[11]), .Cin(full_adder_10_cout), .Saida(Sum[11]), .Cout(full_adder_11_cout));
  full_adder full_adder_12 (.A(B[12]), .B(A[12]), .Cin(full_adder_11_cout), .Saida(Sum[12]), .Cout(full_adder_12_cout));
  full_adder full_adder_13 (.A(B[13]), .B(A[13]), .Cin(full_adder_12_cout), .Saida(Sum[13]), .Cout(full_adder_13_cout));
  full_adder full_adder_14 (.A(B[14]), .B(A[14]), .Cin(full_adder_13_cout), .Saida(Sum[14]), .Cout(full_adder_14_cout));
  full_adder full_adder_15 (.A(B[15]), .B(A[15]), .Cin(full_adder_14_cout), .Saida(Sum[15]), .Cout(Carry));
endmodule

module complemento2 (
  input  [15:0] Input,
  input  Seletor,
  output Carry,
  output [15:0] Saida
);

  wire [15:0] not_1_out, somador_1_sum;

  assign not_1_out = ~Input;  // NOT_Gate not_1, 16 bits wide
  somador somador_1 (.A(not_1_out), .B(16'h1), .Carry(Carry), .Sum(somador_1_sum));
  Multiplexer #(.width(16), .enable("false")) multiplexer_1 (
    .in0(Input), .in1(somador_1_sum), .out(Saida), .sel(Seletor));
endmodule

module somador_final (
  input  [15:0] A,
  input  sinal_A,
  input  [15:0] B,
  input  sinal_B,
  output Cout,
  output [15:0] Saida
);

  wire [15:0] complemento2_1_saida, complemento2_2_saida;

  complemento2 complemento2_1 (.Input(A), .Seletor(sinal_A), .Saida(complemento2_1_saida));  // open: Carry
  complemento2 complemento2_2 (.Input(B), .Seletor(sinal_B), .Saida(complemento2_2_saida));  // open: Carry
  somador somador_1 (.A(complemento2_1_saida), .B(complemento2_2_saida), .Carry(Cout), .Sum(Saida));
endmodule

module MAC (
  input  [7:0] data,
  input  in_2,
  input  write_RAM,
  output Cout,
  output [15:0] Saida
);

  wire clock_1_out, comparator_1_lt, not_1_out, not_2_out;
  wire [3:0] counter_1_q, Incrementador_q, subtractor_1_out;
  wire [7:0] ram_1_data, rom_1_data;
  wire [15:0] bit_extender_1_out, bit_extender_2_out, multiplier_1_out, registrador_q;

  Comparator #(.width(4), .mode("unsigned")) comparator_1 (
    .a(4'b1111), .b(Incrementador_q), .lt(comparator_1_lt));  // open: gt, eq
  Counter #(.width(4), .max('hf)) counter_1 (
    .load(1'b0), .D(4'b0000), .count(1'b1), .Q(counter_1_q), .clk(clock_1_out), .clr(comparator_1_lt));  // open: carry
  Counter #(.width(4), .max('hf)) Incrementador (
    .load(1'b0), .D(4'b0000), .count(1'b1), .Q(Incrementador_q), .clk(clock_1_out), .clr(comparator_1_lt));  // open: carry
  Subtractor #(.width(4)) subtractor_1 (.a(4'b1111), .b(counter_1_q), .out(subtractor_1_out));  // open: bin, bout
  not not_1 (not_1_out, write_RAM);
  RAM #(.addrWidth(4), .bus("separate")) ram_1 (
    .addr(Incrementador_q), .din(data), .data(ram_1_data), .str(write_RAM), .sel(in_2), .clk(clock_1_out),
    .ld(not_1_out));  // open: clr
  ROM #(.addrWidth(4)) rom_1 (.addr(subtractor_1_out), .data(rom_1_data), .sel(1'b1));
  Clock clock_1 (.out(clock_1_out));
  assign bit_extender_1_out = {{8{1'b0}}, ram_1_data};  // Bit_Extender bit_extender_1
  assign bit_extender_2_out = {{8{1'b0}}, rom_1_data};  // Bit_Extender bit_extender_2
  Multiplier #(.width(16)) multiplier_1 (
    .a(bit_extender_1_out), .b(bit_extender_2_out), .out(multiplier_1_out));  // open: cin, cout
  not not_2 (not_2_out, write_RAM);
  somador_final somador_final_1 (
    .A(multiplier_1_out), .sinal_A(1'b0), .B(registrador_q), .sinal_B(1'b0), .Cout(Cout), .Saida(Saida));
  Register #(.width(16)) registrador (
    .D(Saida), .en(not_2_out), .Q(registrador_q), .clk(clock_1_out), .clr(comparator_1_lt));

  // Notes on the sheet:
  //   contents of rom_1 (hex, n*v repeats v):
  //   1 0 10
endmodule
