// Logisim project MIPS.circ as structural Verilog: 20 circuits, main circuit CPU
module DATAPATH (
  input  [31:0] DOUT_ROM,
  input  [6:0] DOUT_TEC,
  input  [31:0] DOUT_BUS,
  input  [1:0] SEL_OP1,
  input  SEL_OP2,
  input  WR_ACC,
  input  SEL_ULA,
  input  clock,
  output [5:0] OPCODE,
  output [25:0] ADD_IMED,
  output [31:0] ACC,
  output [31:0] DIN_BUS
);

  wire [31:0] bit_extender_1_out, bit_extender_2_out, IR_q, multiplexer_1_out, multiplexer_2_out,
       ULA_ula_output;

  assign bit_extender_1_out = {{25{1'b0}}, DOUT_TEC};  // Bit_Extender bit_extender_1
  Multiplexer #(.width(32), .enable("false")) multiplexer_1 (
    .in0(DOUT_BUS), .in1(bit_extender_2_out), .out(multiplexer_1_out), .sel(SEL_OP2));
  Register #(.width(32)) IR (.D(DOUT_ROM), .en(1'b1), .Q(IR_q), .clk(clock), .clr(1'b0));
  IR_bits_distributor ir_bits_distributor_1 (.Input(IR_q), .ADDRESS(ADD_IMED), .OPCODE(OPCODE));
  ULA ULA (.Input_acc(ACC), .Input_mux(multiplexer_1_out), .SEL_ULA(SEL_ULA), .ULA_Output(ULA_ula_output));
  assign bit_extender_2_out = {{6{1'b0}}, ADD_IMED};  // Bit_Extender bit_extender_2
  Multiplexer #(.select(2), .width(32), .enable("false")) multiplexer_2 (
    .in0(DOUT_BUS), .in1(bit_extender_2_out), .in2(ULA_ula_output), .in3(bit_extender_1_out),
    .out(multiplexer_2_out), .sel(SEL_OP1));
  Register #(.width(32)) u_ACC (.D(multiplexer_2_out), .en(WR_ACC), .Q(ACC), .clk(clock), .clr(1'b0));

  assign DIN_BUS = ACC;
endmodule

module ULA (
  input  [31:0] Input_acc,
  input  [31:0] Input_mux,
  input  SEL_ULA,
  output [31:0] ULA_Output
);

  wire [31:0] adder_1_out, subtractor_1_out;

  Adder #(.width(32)) adder_1 (.a(Input_acc), .b(Input_mux), .out(adder_1_out));  // open: cin, cout
  Subtractor #(.width(32)) subtractor_1 (.a(Input_acc), .b(Input_mux), .out(subtractor_1_out));  // open: bin, bout
  Multiplexer #(.width(32), .enable("false")) multiplexer_1 (
    .in0(adder_1_out), .in1(subtractor_1_out), .out(ULA_Output), .sel(SEL_ULA));
endmodule

// IR_dsitributor
module IR_bits_distributor (
  input  [31:0] Input,
  output [25:0] ADDRESS,
  output [5:0] OPCODE
);


  assign ADDRESS = Input[25:0];
  assign OPCODE = Input[31:26];
endmodule

module CONTROL_EN_RAM (
  input  OP31,
  input  OP30,
  input  OP29,
  input  OP28,
  input  OP27,
  input  OP26,
  output EN_RAM
);

  wire and_1_out, and_2_out, and_3_out, and_4_out, not_1_out, not_2_out, not_3_out, not_4_out, not_5_out,
       not_6_out, not_7_out, not_8_out, not_9_out, not_10_out, not_11_out, not_12_out, not_13_out,
       not_14_out, not_15_out, not_16_out, not_17_out, not_18_out, not_19_out;

  not not_1 (not_1_out, OP27);
  not not_2 (not_2_out, OP28);
  not not_3 (not_3_out, OP29);
  not not_4 (not_4_out, OP30);
  not not_5 (not_5_out, OP31);
  not not_6 (not_6_out, OP26);
  not not_7 (not_7_out, OP28);
  not not_8 (not_8_out, OP29);
  not not_9 (not_9_out, OP30);
  not not_10 (not_10_out, OP31);
  not not_11 (not_11_out, OP26);
  not not_12 (not_12_out, OP27);
  not not_13 (not_13_out, OP29);
  not not_14 (not_14_out, OP30);
  not not_15 (not_15_out, OP31);
  not not_16 (not_16_out, OP26);
  not not_17 (not_17_out, OP29);
  not not_18 (not_18_out, OP30);
  not not_19 (not_19_out, OP31);
  and and_1 (and_1_out, OP26, not_1_out, not_2_out, not_3_out, not_4_out, not_5_out);
  and and_2 (and_2_out, not_6_out, OP27, not_7_out, not_8_out, not_9_out, not_10_out);
  and and_3 (and_3_out, not_11_out, not_12_out, OP28, not_13_out, not_14_out, not_15_out);
  and and_4 (and_4_out, not_16_out, OP27, OP28, not_17_out, not_18_out, not_19_out);
  or or_1 (EN_RAM, and_1_out, and_2_out, and_3_out, and_4_out);
endmodule

module CONTROL_WR_RAM (
  input  OP31,
  input  OP30,
  input  OP29,
  input  OP28,
  input  OP27,
  input  OP26,
  output WR_RAM
);

  wire not_1_out, not_2_out, not_3_out, not_4_out, not_5_out;

  not not_1 (not_1_out, OP27);
  not not_2 (not_2_out, OP28);
  not not_3 (not_3_out, OP29);
  not not_4 (not_4_out, OP30);
  not not_5 (not_5_out, OP31);
  and and_1 (WR_RAM, OP26, not_1_out, not_2_out, not_3_out, not_4_out, not_5_out);
endmodule

module CONTROL_RD_RAM (
  input  OP31,
  input  OP30,
  input  OP29,
  input  OP28,
  input  OP27,
  input  OP26,
  output RD_RAM
);

  wire and_1_out, and_2_out, and_3_out, not_1_out, not_2_out, not_3_out, not_4_out, not_5_out, not_6_out,
       not_7_out, not_8_out, not_9_out, not_10_out, not_11_out, not_12_out, not_13_out, not_14_out;

  not not_1 (not_1_out, OP26);
  not not_2 (not_2_out, OP28);
  not not_3 (not_3_out, OP29);
  not not_4 (not_4_out, OP30);
  not not_5 (not_5_out, OP31);
  not not_6 (not_6_out, OP26);
  not not_7 (not_7_out, OP27);
  not not_8 (not_8_out, OP29);
  not not_9 (not_9_out, OP30);
  not not_10 (not_10_out, OP31);
  not not_11 (not_11_out, OP26);
  not not_12 (not_12_out, OP29);
  not not_13 (not_13_out, OP30);
  not not_14 (not_14_out, OP31);
  and and_1 (and_1_out, not_1_out, OP27, not_2_out, not_3_out, not_4_out, not_5_out);
  and and_2 (and_2_out, not_6_out, not_7_out, OP28, not_8_out, not_9_out, not_10_out);
  and and_3 (and_3_out, not_11_out, OP27, OP28, not_12_out, not_13_out, not_14_out);
  or or_1 (RD_RAM, and_1_out, and_2_out, and_3_out);
endmodule

module CONTROL_WR_ACC (
  input  OP31,
  input  OP30,
  input  OP29,
  input  OP28,
  input  OP27,
  input  OP26,
  output WR_ACC
);

  wire not_1_out, not_2_out, not_3_out, not_4_out, or_1_out, or_2_out, or_3_out, or_4_out;

  not not_1 (not_1_out, OP26);
  not not_2 (not_2_out, OP29);
  not not_3 (not_3_out, OP27);
  not not_4 (not_4_out, OP29);
  or or_1 (or_1_out, OP26, OP27, OP28, OP29, OP30, OP31);
  or or_2 (or_2_out, not_1_out, OP27, OP28, OP29, OP30, OP31);
  or or_3 (or_3_out, OP26, OP27, OP28, not_2_out, OP30, OP31);
  or or_4 (or_4_out, OP26, not_3_out, OP28, not_4_out, OP30, OP31);
  and and_1 (WR_ACC, or_1_out, or_2_out, or_3_out, or_4_out);
endmodule

module CONTROL_SEL_OP1 (
  input  OP31,
  input  OP30,
  input  OP29,
  input  OP28,
  input  OP27,
  input  OP26,
  output [1:0] SEL_OP1
);

  wire and_1_out, and_2_out, and_3_out, and_4_out, and_5_out, and_6_out, and_7_out, and_8_out, and_9_out,
       not_1_out, not_2_out, not_3_out, not_4_out, not_5_out, not_6_out, not_7_out, not_8_out, not_9_out,
       not_10_out, not_11_out, not_12_out, not_13_out, not_14_out, not_15_out, not_16_out, not_17_out,
       not_18_out, not_19_out, not_20_out, not_21_out, not_22_out, not_23_out, not_24_out, not_25_out,
       not_26_out, not_27_out, not_28_out, not_29_out, not_30_out, not_31_out, not_32_out, not_33_out,
       not_34_out, not_35_out, not_36_out, not_37_out;

  not not_1 (not_1_out, OP28);
  not not_2 (not_2_out, OP29);
  not not_3 (not_3_out, OP30);
  not not_4 (not_4_out, OP31);
  not not_5 (not_5_out, OP27);
  not not_6 (not_6_out, OP28);
  not not_7 (not_7_out, OP30);
  not not_8 (not_8_out, OP31);
  not not_9 (not_9_out, OP26);
  not not_10 (not_10_out, OP27);
  not not_11 (not_11_out, OP29);
  not not_12 (not_12_out, OP30);
  not not_13 (not_13_out, OP31);
  not not_14 (not_14_out, OP26);
  not not_15 (not_15_out, OP29);
  not not_16 (not_16_out, OP30);
  not not_17 (not_17_out, OP31);
  not not_18 (not_18_out, OP27);
  not not_19 (not_19_out, OP29);
  not not_20 (not_20_out, OP30);
  not not_21 (not_21_out, OP31);
  not not_22 (not_22_out, OP29);
  not not_23 (not_23_out, OP30);
  not not_24 (not_24_out, OP31);
  not not_25 (not_25_out, OP26);
  not not_26 (not_26_out, OP27);
  not not_27 (not_27_out, OP28);
  not not_28 (not_28_out, OP30);
  not not_29 (not_29_out, OP31);
  not not_30 (not_30_out, OP27);
  not not_31 (not_31_out, OP28);
  not not_32 (not_32_out, OP30);
  not not_33 (not_33_out, OP31);
  not not_34 (not_34_out, OP26);
  not not_35 (not_35_out, OP28);
  not not_36 (not_36_out, OP30);
  not not_37 (not_37_out, OP31);
  and and_1 (and_1_out, OP26, OP27, not_1_out, not_2_out, not_3_out, not_4_out);
  and and_2 (and_2_out, OP26, not_5_out, not_6_out, OP29, not_7_out, not_8_out);
  and and_3 (and_3_out, not_9_out, not_10_out, OP28, not_11_out, not_12_out, not_13_out);
  and and_4 (and_4_out, not_14_out, OP27, OP28, not_15_out, not_16_out, not_17_out);
  and and_5 (and_5_out, OP26, not_18_out, OP28, not_19_out, not_20_out, not_21_out);
  and and_6 (and_6_out, OP26, OP27, OP28, not_22_out, not_23_out, not_24_out);
  and and_7 (and_7_out, not_25_out, not_26_out, not_27_out, OP29, not_28_out, not_29_out);
  and and_8 (and_8_out, OP26, not_30_out, not_31_out, OP29, not_32_out, not_33_out);
  and and_9 (and_9_out, not_34_out, OP27, not_35_out, OP29, not_36_out, not_37_out);
  or or_1 (SEL_OP1[0], and_1_out, and_2_out);
  or or_2 (SEL_OP1[1], and_3_out, and_4_out, and_5_out, and_6_out, and_7_out, and_8_out, and_9_out);
endmodule

module CONTROL_SEL_OP2 (
  input  OP31,
  input  OP30,
  input  OP29,
  input  OP28,
  input  OP27,
  input  OP26,
  output SEL_OP2
);

  wire not_1_out, not_2_out, not_3_out, or_1_out, or_2_out;

  not not_1 (not_1_out, OP28);
  not not_2 (not_2_out, OP27);
  not not_3 (not_3_out, OP28);
  or or_1 (or_1_out, OP26, OP27, not_1_out, OP29, OP30, OP31);
  or or_2 (or_2_out, OP26, not_2_out, not_3_out, OP29, OP30, OP31);
  and and_1 (SEL_OP2, or_1_out, or_2_out);
endmodule

module CONTROL_SEL_ULA (
  input  OP31,
  input  OP30,
  input  OP29,
  input  OP28,
  input  OP27,
  input  OP26,
  output SEL_ULA
);

  wire and_1_out, and_2_out, not_1_out, not_2_out, not_3_out, not_4_out, not_5_out, not_6_out, not_7_out;

  not not_1 (not_1_out, OP26);
  not not_2 (not_2_out, OP29);
  not not_3 (not_3_out, OP30);
  not not_4 (not_4_out, OP31);
  not not_5 (not_5_out, OP29);
  not not_6 (not_6_out, OP30);
  not not_7 (not_7_out, OP31);
  and and_1 (and_1_out, not_1_out, OP27, OP28, not_2_out, not_3_out, not_4_out);
  and and_2 (and_2_out, OP26, OP27, OP28, not_5_out, not_6_out, not_7_out);
  or or_1 (SEL_ULA, and_1_out, and_2_out);
endmodule

module CONTROL_LOGIC (
  input  [5:0] OPCODE,
  output SEL_JMP,
  output EN_MON,
  output EN_TEC,
  output SEL_ULA,
  output SEL_OP2,
  output [1:0] SEL_OP1,
  output WR_ACC,
  output RD_RAM,
  output WR_RAM,
  output EN_PC,
  output EN_RAM
);

  CONTROL_EN_MON control_en_mon_1 (
    .OP31(OPCODE[5]), .OP30(OPCODE[4]), .OP29(OPCODE[3]), .OP28(OPCODE[2]), .OP27(OPCODE[1]),
    .OP26(OPCODE[0]), .EN_MON(EN_MON));
  CONTROL_EN_TEC control_en_tec_1 (
    .OP31(OPCODE[5]), .OP30(OPCODE[4]), .OP29(OPCODE[3]), .OP28(OPCODE[2]), .OP27(OPCODE[1]),
    .OP26(OPCODE[0]), .EN_TEC(EN_TEC));
  CONTROL_SEL_ULA control_sel_ula_1 (
    .OP31(OPCODE[5]), .OP30(OPCODE[4]), .OP29(OPCODE[3]), .OP28(OPCODE[2]), .OP27(OPCODE[1]),
    .OP26(OPCODE[0]), .SEL_ULA(SEL_ULA));
  CONTROL_SEL_OP2 control_sel_op2_1 (
    .OP31(OPCODE[5]), .OP30(OPCODE[4]), .OP29(OPCODE[3]), .OP28(OPCODE[2]), .OP27(OPCODE[1]),
    .OP26(OPCODE[0]), .SEL_OP2(SEL_OP2));
  CONTROL_SEL_OP1 control_sel_op1_1 (
    .OP31(OPCODE[5]), .OP30(OPCODE[4]), .OP29(OPCODE[3]), .OP28(OPCODE[2]), .OP27(OPCODE[1]),
    .OP26(OPCODE[0]), .SEL_OP1(SEL_OP1));
  CONTROL_WR_ACC control_wr_acc_1 (
    .OP31(OPCODE[5]), .OP30(OPCODE[4]), .OP29(OPCODE[3]), .OP28(OPCODE[2]), .OP27(OPCODE[1]),
    .OP26(OPCODE[0]), .WR_ACC(WR_ACC));
  CONTROL_RD_RAM control_rd_ram_1 (
    .OP31(OPCODE[5]), .OP30(OPCODE[4]), .OP29(OPCODE[3]), .OP28(OPCODE[2]), .OP27(OPCODE[1]),
    .OP26(OPCODE[0]), .RD_RAM(RD_RAM));
  CONTROL_WR_RAM control_wr_ram_1 (
    .OP31(OPCODE[5]), .OP30(OPCODE[4]), .OP29(OPCODE[3]), .OP28(OPCODE[2]), .OP27(OPCODE[1]),
    .OP26(OPCODE[0]), .WR_RAM(WR_RAM));
  CONTROL_EN_RAM control_en_ram_1 (
    .OP31(OPCODE[5]), .OP30(OPCODE[4]), .OP29(OPCODE[3]), .OP28(OPCODE[2]), .OP27(OPCODE[1]),
    .OP26(OPCODE[0]), .EN_RAM(EN_RAM));
  CONTROL_SEL_JMP control_sel_jmp_1 (
    .OP31(OPCODE[5]), .OP30(OPCODE[4]), .OP29(OPCODE[3]), .OP28(OPCODE[2]), .OP27(OPCODE[1]),
    .OP26(OPCODE[0]), .EN_MON(SEL_JMP));

  assign EN_PC = 1'b1;
endmodule

module PROCESSOR (
  input  CLK,
  input  [6:0] DOUT_TEC,
  input  [31:0] DOUT_BUS,
  input  [31:0] DOUT_ROM,
  output SEL_MON,
  output EN_TEC,
  output [31:0] ACC,
  output RD_RAM,
  output WR_RAM,
  output EN_RAM,
  output [31:0] DIN_BUS,
  output [23:0] ADD_IMED,
  output [23:0] ADD_ROM
);

  wire CONTROL_sel_op2, CONTROL_sel_ula, CONTROL_wr_acc;
  wire [1:0] CONTROL_sel_op1;
  wire [5:0] DATAPATH_opcode;
  wire [25:0] CONTROL_rom_add, DATAPATH_add_imed;

  DATAPATH DATAPATH (
    .ADD_IMED(DATAPATH_add_imed), .SEL_OP1(CONTROL_sel_op1), .SEL_OP2(CONTROL_sel_op2),
    .WR_ACC(CONTROL_wr_acc), .DIN_BUS(DIN_BUS), .SEL_ULA(CONTROL_sel_ula), .clock(CLK),
    .OPCODE(DATAPATH_opcode), .DOUT_ROM(DOUT_ROM), .ACC(ACC), .DOUT_BUS(DOUT_BUS), .DOUT_TEC(DOUT_TEC));
  _26_TO_24_BITS u_26_to_24_bits_1 (.INPUT(DATAPATH_add_imed), .OUTPUT(ADD_IMED));
  CONTROL CONTROL (
    .ROM_ADD(CONTROL_rom_add), .SEL_ULA(CONTROL_sel_ula), .SEL_OP2(CONTROL_sel_op2),
    .SEL_OP1(CONTROL_sel_op1), .WR_ACC(CONTROL_wr_acc), .RD_RAM(RD_RAM), .WR_RAM(WR_RAM), .EN_RAM(EN_RAM),
    .OPCODE(DATAPATH_opcode), .ADD_IMED(DATAPATH_add_imed), .clk(CLK), .EN_TEC(EN_TEC), .SEL_MON(SEL_MON));
  _26_TO_24_BITS u_26_to_24_bits_2 (.INPUT(CONTROL_rom_add), .OUTPUT(ADD_ROM));
endmodule

module CONTROL (
  input  clk,
  input  [25:0] ADD_IMED,
  input  [5:0] OPCODE,
  output SEL_MON,
  output EN_TEC,
  output SEL_ULA,
  output SEL_OP2,
  output [1:0] SEL_OP1,
  output WR_ACC,
  output RD_RAM,
  output WR_RAM,
  output EN_RAM,
  output [25:0] ROM_ADD
);

  wire control_logic_1_en_pc, control_logic_1_sel_jmp;
  wire [25:0] adder_1_out, PC_q;

  CONTROL_LOGIC control_logic_1 (
    .SEL_ULA(SEL_ULA), .SEL_OP2(SEL_OP2), .SEL_OP1(SEL_OP1), .WR_ACC(WR_ACC), .RD_RAM(RD_RAM),
    .WR_RAM(WR_RAM), .EN_PC(control_logic_1_en_pc), .EN_RAM(EN_RAM), .OPCODE(OPCODE), .EN_TEC(EN_TEC),
    .EN_MON(SEL_MON), .SEL_JMP(control_logic_1_sel_jmp));
  Adder #(.width(26)) adder_1 (.a(ROM_ADD), .b(26'h1), .out(adder_1_out));  // open: cin, cout
  Register #(.width(26)) PC (.D(adder_1_out), .en(control_logic_1_en_pc), .Q(PC_q), .clk(clk));  // open: clr
  Multiplexer #(.width(26), .enable("false")) multiplexer_1 (
    .in0(ADD_IMED), .in1(PC_q), .out(ROM_ADD), .sel(control_logic_1_sel_jmp));
endmodule

module _26_TO_24_BITS (
  input  [25:0] INPUT,
  output [23:0] OUTPUT
);


  assign OUTPUT = INPUT[23:0];
endmodule

module CPU (
  input  CLOCK,
  input  [6:0] DOUT_TEC,
  output EN_MON,
  output EN_TEC,
  output [31:0] ACC
);

  wire processor_1_en_ram, processor_1_rd_ram, processor_1_wr_ram;
  wire [23:0] processor_1_add_imed, processor_1_add_rom;
  wire [31:0] processor_1_din_bus, ram_1_data, rom_1_data;

  RAM #(.addrWidth(24), .dataWidth(32), .bus("separate")) ram_1 (
    .addr(processor_1_add_imed), .din(processor_1_din_bus), .data(ram_1_data), .str(processor_1_wr_ram),
    .sel(processor_1_en_ram), .clk(CLOCK), .ld(processor_1_rd_ram));  // open: clr
  PROCESSOR processor_1 (
    .RD_RAM(processor_1_rd_ram), .WR_RAM(processor_1_wr_ram), .CLK(CLOCK), .DOUT_ROM(rom_1_data),
    .ADD_IMED(processor_1_add_imed), .DOUT_BUS(ram_1_data), .DIN_BUS(processor_1_din_bus),
    .EN_RAM(processor_1_en_ram), .ADD_ROM(processor_1_add_rom), .ACC(ACC), .DOUT_TEC(DOUT_TEC),
    .EN_TEC(EN_TEC), .SEL_MON(EN_MON));
  ROM #(.addrWidth(24), .dataWidth(32)) rom_1 (.addr(processor_1_add_rom), .data(rom_1_data), .sel(1'b1));

  // Notes on the sheet:
  //   contents of rom_1 (hex, n*v repeats v):
  //   c000005 4000000 c000003 4000001 10000000 4000002 18000001 14000006 1c000003 4000004 8000002 1c000004
endmodule

module TOPLEVEL (
  input  CLK
);

  wire CPU_en_mon, CPU_en_tec;
  wire [6:0] keyboard_1_data, n32_to_7_bits_1_ouput;
  wire [31:0] CPU_acc;

  _32_TO_7_BITS u_32_to_7_bits_1 (.INPUT(CPU_acc), .OUPUT(n32_to_7_bits_1_ouput));
  TTY tty_1 (.data(n32_to_7_bits_1_ouput), .clk(CLK), .we(CPU_en_mon));  // open: clr
  Keyboard keyboard_1 (.clk(CLK), .re(CPU_en_tec), .data(keyboard_1_data));  // open: clr, avail
  CPU CPU (.EN_MON(CPU_en_mon), .ACC(CPU_acc), .CLOCK(CLK), .DOUT_TEC(keyboard_1_data), .EN_TEC(CPU_en_tec));
endmodule

module CONTROL_EN_TEC (
  input  OP31,
  input  OP30,
  input  OP29,
  input  OP28,
  input  OP27,
  input  OP26,
  output EN_TEC
);

  wire not_1_out, not_2_out, not_3_out, not_4_out;

  not not_1 (not_1_out, OP27);
  not not_2 (not_2_out, OP28);
  not not_3 (not_3_out, OP30);
  not not_4 (not_4_out, OP31);
  and and_1 (EN_TEC, OP26, not_1_out, not_2_out, OP29, not_3_out, not_4_out);
endmodule

module CONTROL_EN_MON (
  input  OP31,
  input  OP30,
  input  OP29,
  input  OP28,
  input  OP27,
  input  OP26,
  output EN_MON
);

  wire not_1_out, not_2_out, not_3_out, not_4_out;

  not not_1 (not_1_out, OP26);
  not not_2 (not_2_out, OP28);
  not not_3 (not_3_out, OP30);
  not not_4 (not_4_out, OP31);
  and and_1 (EN_MON, not_1_out, OP27, not_2_out, OP29, not_3_out, not_4_out);
endmodule

module CONTROL_SEL_JMP (
  input  OP31,
  input  OP30,
  input  OP29,
  input  OP28,
  input  OP27,
  input  OP26,
  output EN_MON
);

  wire not_1_out, not_2_out, not_3_out, not_4_out, not_5_out;

  not not_1 (not_1_out, OP26);
  not not_2 (not_2_out, OP27);
  not not_3 (not_3_out, OP28);
  not not_4 (not_4_out, OP30);
  not not_5 (not_5_out, OP31);
  and and_1 (EN_MON, not_1_out, not_2_out, not_3_out, OP29, not_4_out, not_5_out);
endmodule

module _32_TO_7_BITS (
  input  [31:0] INPUT,
  output [6:0] OUPUT
);


  assign OUPUT = INPUT[6:0];
endmodule
